# Fritzing sketch radio (saved by Fritzing 0.9.5d)
breadboards: 1

parts:
  WeMos_D1_R1 = WeMos D1 R2
  Компонент1 = Adafruit MAX98357A I2S 3W Class D Amplifier [part_number="Adafruit #3006"]
  S1 = Pushbutton [package=THT]
  R1 = Resistor [tolerance=±5% power=0.25 resistance=10k package=THT]
  RE1 = Rotary Encoder [package=THT]
  SP1 = SPEAKER [package=pcb_mount_speaker]
  part = Resistor [tolerance=±5% resistance=4.7 package=THT]

nets:
  N1: WeMos_D1_R1.D0/RX, Компонент1.DIN
  N2: WeMos_D1_R1.D4, Компонент1.LRCLK
  N3: WeMos_D1_R1.(D6), S1.leg0, R1.Pin_0
  N4: WeMos_D1_R1.D8, Компонент1.BCLK
  N5: WeMos_D1_R1.A0, RE1.EncoderPinC
  GND: WeMos_D1_R1.GND, Компонент1.GND, Компонент1.GAIN, R1.Pin_1, RE1.EncoderPinA
  N6: WeMos_D1_R1.3.3V, S1.leg1, part.Pin_1
  N7: Компонент1.VO-, SP1.+
  N8: Компонент1.VO+, SP1.-
  N9: RE1.EncoderPinB, part.Pin_0

custom parts:
  WeMos D1 R2: The D1 R2 is a mini wifi board based on the ESP-8266EX.
  Adafruit MAX98357A I2S 3W Class D Amplifier: Listen to this good news - we now have an all in one digital audio amp breakout board that works incredibly well with the Raspberry Pi! If you're looking for an easy and low cost way to get you digital sound files bumpin' then the MAX08357 I2S Amp Breakout is for you. It takes standard I2S digital audio input and, not only decodes it into analog, but also amplifies it directly into a speaker.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
